// Digital circuit t2h.dig as structural Verilog
// The T2H processor is a one clock Harvard 16 bit implementation of a small subset of the Inmos Transputer
module t2h (
  input  reset,
  input  clock,
  input  [7:0] Inst,
  input  [15:0] dIn,
  output [15:0] I,
  output [15:0] Addr,
  output wr,
  output rd,
  output [15:0] dOut
);

  wire add_3_s, clrO, eA, eB, eC, eW, negO, s_plus, sA, sAddr, sB, sW;
  wire [1:0] sDout, sI;
  wire [3:0] sALU;
  wire [7:0] multiplexer_1_out, not_1_out;
  wire [11:0] multiplexer_3_out;
  wire [15:0] A, add_2_s, add_4_s, B, C, I_plus_1, multiplexer_2_out, multiplexer_4_out, multiplexer_5_out,
       multiplexer_6_out, multiplexer_7_out, multiplexer_8_out, W_q;
  wire [15:4] x;

  Multiplexer #(.Bits(8)) multiplexer_1 (.sel(negO), .in_0(x[11:4]), .in_1(not_1_out), .out(multiplexer_1_out));
  assign not_1_out = ~x[11:4];  // Not not_1, 8 bits wide
  Multiplexer #(.Bits(16), .Selector_Bits(4)) multiplexer_2 (
    .sel(sALU), .out(multiplexer_2_out));  // open: in_0, in_1, in_2, in_3, in_4, in_5, in_6, in_7, in_8, in_9, in_10, in_11, in_12, in_13, in_14, in_15
  Multiplexer #(.Bits(12)) multiplexer_3 (
    .sel(clrO), .in_0({12{1'b0}}), .in_1({multiplexer_1_out, Inst[3:0]}), .out(multiplexer_3_out));
  Register #(.Bits(12)) O (.D(multiplexer_3_out), .C(clock), .en(1'b1), .Q(x));
  Add #(.Bits(16)) add_1 (.a(I), .b({16{1'b0}}), .c_i(1'b1), .s(I_plus_1));  // open: c_o
  Add add_2 (.a(I[0]), .b(Inst[0]), .c_i(1'b1), .s(add_2_s[0]));  // open: c_o
  Add add_3 (.a(Inst[0]), .b(W_q[0]), .c_i(1'b0), .s(add_3_s));  // open: c_o
  Multiplexer #(.Bits(16), .Selector_Bits(2)) multiplexer_4 (
    .sel(sI), .in_0(I_plus_1), .in_1(add_2_s), .in_2(A), .in_3(dIn), .out(multiplexer_4_out));
  Multiplexer multiplexer_5 (.sel(sA), .in_0(dIn[0]), .in_1(multiplexer_2_out[0]), .out(multiplexer_5_out[0]));
  Multiplexer multiplexer_6 (.sel(sB), .in_0(A[0]), .in_1(C[0]), .out(multiplexer_6_out[0]));
  Multiplexer multiplexer_7 (.sel(sW), .in_0(add_3_s), .in_1(A[0]), .out(multiplexer_7_out[0]));
  Multiplexer #(.Bits(16)) multiplexer_8 (.sel(s_plus), .in_0(W_q), .in_1(A), .out(multiplexer_8_out));
  Register #(.Bits(16)) u_I (.D(multiplexer_4_out), .C(clock), .en(1'b1), .Q(I));
  Register #(.Bits(16)) W (.D(multiplexer_7_out), .C(clock), .en(eW), .Q(W_q));
  Add #(.Bits(16)) add_4 (.a(multiplexer_8_out), .b({x[14:4], Inst[3:0], 1'b0}), .c_i(1'b0), .s(add_4_s));  // open: c_o
  Register #(.Bits(16)) u_A (.D(multiplexer_5_out), .C(clock), .en(eA), .Q(A));
  Register #(.Bits(16)) u_B (.D(multiplexer_6_out), .C(clock), .en(eB), .Q(B));
  Register #(.Bits(16)) u_C (.D(B), .C(clock), .en(eC), .Q(C));
  Multiplexer #(.Bits(16)) multiplexer_9 (.sel(sAddr), .in_0(W_q), .in_1(add_4_s), .out(Addr));
  Multiplexer #(.Bits(16), .Selector_Bits(2)) multiplexer_10 (
    .sel(sDout), .in_0(A), .in_1(B), .in_2(I_plus_1), .in_3(I_plus_1), .out(dOut));
  // Pins of 1 and 16 bits meet at I
  // Pins of 1 and 16 bits meet at dIn
  // Pins of 1 and 16 bits meet at multiplexer_5_out
  // Pins of 1 and 16 bits meet at A
  // Pins of 1 and 16 bits meet at multiplexer_6_out
  // Pins of 1 and 16 bits meet at C
  // Pins of 1 and 16 bits meet at multiplexer_7_out
  // Pins of 1 and 16 bits meet at W_q
  // Pins of 8 and 12 bits meet at x
  // Pins of 1 and 16 bits meet at add_2_s
  // Pins of 1 and 16 bits meet at {x, Inst[3:0]}
  // Pins of 1 and 16 bits meet at multiplexer_2_out

  // Other names for the same wires on the sheet: x[3:0] = Inst[3:0]

  // Notes on the sheet:
  //   I: program counter
  //   Addr: Data memory address
  //   wr: write to memory
  //   rd: indicates a read cycle from memory
  //   Inst: instruction to be executed
  //   dIn: data from memory
  //   dOut: data output to memory
endmodule
