// Digital circuit controlUnit.dig as structural Verilog
// generates control signals for datapath
module controlUnit (
  input  clock,
  input  reset,
  input  [15:0] dIn,
  input  alt,
  input  NE,
  input  GE,
  output wr,
  output rd,
  output sign,
  output word,
  output sub,
  output \logic ,
  output [1:0] logSelect,
  output [11:0] topImm,
  output even,
  output const2,
  output selImm,
  output selConst,
  output Azero,
  output we,
  output [3:0] Rw,
  output [3:0] Ra,
  output [3:0] Rb,
  output selRd,
  output slt,
  output immLow
);

  wire and_1_out, and_2_out, and_3_out, and_5_out, and_7_out, and_8_out, and_9_out, and_10_out, and_11_out,
       and_12_out, and_13_out, and_18_out, and_20_out, and_21_out, branch, cond, d_ff_1_q, d_ff_2_q, E, EJ,
       F, FJorBT, imm, IR2, IR3, multiplexer_2_out, or_1_out, or_5_out, or_11_out, prefix_q, xor_1_out, zD,
       zS1, zS2;
  wire [11:0] multiplexer_1_out;
  wire [15:8] IR_q;

  and and_1 (and_1_out, E, zS1);
  Multiplexer #(.Bits(12)) multiplexer_1 (
    .sel(d_ff_2_q), .in_0({IR_q, Rb}), .in_1({12{1'b0}}), .out(multiplexer_1_out));
  and and_2 (and_2_out, ~dIn[0], ~dIn[1], ~dIn[2], ~dIn[3], F);  // And
  and and_3 (and_3_out, ~IR3, ~IR2, ~logSelect[1], ~logSelect[0]);  // And
  Multiplexer multiplexer_2 (.sel(logSelect[0]), .in_0(NE), .in_1(GE), .out(multiplexer_2_out));
  xor xor_1 (xor_1_out, multiplexer_2_out, alt);
  D_FF d_ff_1 (.D(reset), .C(clock), .Q(d_ff_1_q));  // open: nQ
  Register #(.Bits(16)) IR (.D(dIn), .C(clock), .en(F), .Q({IR_q, Rb, IR3, IR2, logSelect}));
  Register #(.Bits(12)) IM (.D(multiplexer_1_out), .C(clock), .en(F), .Q(topImm));
  D_FF fetch (.D(or_1_out), .C(clock), .Q(F), .nQ(E));
  // Probe IR on {IR_q, Rb, IR3, IR2, logSelect}
  or or_1 (or_1_out, E, d_ff_1_q, and_2_out);
  Register prefix (.D(and_3_out), .C(clock), .en(F), .Q(prefix_q));
  // Probe IM on topImm
  D_FF d_ff_2 (.D(E), .C(clock), .Q(d_ff_2_q));  // open: nQ
  and and_4 (zS2, E, ~Rb[0], ~Rb[1], ~Rb[2], ~Rb[3]);  // And
  or or_2 (imm, prefix_q, ~IR3);  // Or
  and and_5 (and_5_out, ~IR3, ~IR2, ~logSelect[1], logSelect[0]);  // And
  and and_6 (branch, ~IR3, ~IR2, logSelect[1]);  // And
  // Probe fetch on F
  D_FF d_ff_3 (.D(xor_1_out), .C(clock), .Q(cond));  // open: nQ
  and and_7 (and_7_out, E, ~IR2, ~logSelect[1], ~logSelect[0]);  // And
  and and_8 (and_8_out, E, ~IR3, IR2);  // And
  and and_9 (and_9_out, and_5_out, alt);
  or or_3 (selRd, and_7_out, and_8_out);
  and and_10 (and_10_out, F, ~and_9_out);  // And
  and and_11 (and_11_out, F, ~d_ff_1_q);  // And
  or or_4 (Azero, d_ff_1_q, and_1_out);
  and and_12 (and_12_out, ~EJ, E, imm);  // And
  and and_13 (and_13_out, F, ~FJorBT);  // And
  or or_5 (or_5_out, branch, zD);
  r0 r0_1 (.rin(IR_q[11:8]), .pc(or_11_out), .rout(Ra), .z(zS1));
  and and_14 (wr, E, ~IR3, IR2, logSelect[1]);  // And
  or or_6 (rd, F, selRd);
  and and_15 (sub, E, ~IR2, logSelect[1]);  // And
  and and_16 (\logic , E, IR3, IR2);
  nand nand_1 (we, E, or_5_out);
  r0 r0_2 (.rin(IR_q[15:12]), .pc(F), .rout(Rw), .z(zD));
  and and_17 (slt, E, ~IR2, logSelect[1], logSelect[0]);  // And
  and and_18 (and_18_out, F, ~IR3, logSelect[1]);  // And
  and and_19 (EJ, E, and_5_out);
  and and_20 (and_20_out, F, and_5_out);
  and and_21 (and_21_out, F, branch, cond);
  or or_7 (const2, and_11_out, EJ);
  or or_8 (selImm, FJorBT, and_12_out);
  or or_9 (selConst, EJ, and_13_out, zS2);
  or or_10 (immLow, and_18_out, wr);
  or or_11 (or_11_out, and_10_out, EJ);
  or or_12 (FJorBT, and_20_out, and_21_out);
  not not_1 (sign, IR3);

  assign even = const2;
  assign word = logSelect[0];

  // Other names for the same wires on the sheet: IR0 = logSelect[0]; IR1 = logSelect[1]

  // Notes on the sheet:
  //   clock: controls internal registers
  //   reset: when high forces the PC to 0x0000
  //   dIn: data from memory
  //   alt: immediate value indicates alternative instruction in lowest bit
  //   NE: A ~= B
  //   GE: A >= B
  //   wr: memory write cycle
  //   rd: memory read cycle
  //   sign: not LBU
  //   word: not SB, LB or LBU
  //   sub: change addition to subtraction
  //   logic: select logic operation instead of addition
  //   logSelect: selects between shift right, AND, OR, XOR
  //   topImm: saved from prefix instruction
  //   even: forces bottom bit of immediate to 0
  //   const2: changes constant from 0 to 2
  //   selImm: B is immediate
  //   selConst: B is a constant
  //   Azero: force A to 0
  //   we: updates register Rw
  //   Rw: register to be written
  //   Ra: first register to read
  //   Rb: second register to read
  //   selRd: selects betweenALU result and memory for write back
  //   slt: ignores ALU result and use GE?0x0000:0x0001
  //   immLow: selects either field rS2 or rD for the 4 lower bits of immediate
endmodule
