// Digital circuit drv16.dig as structural Verilog
// 16 bit processor which is compatible at the assembly language level with RISC-V
module drv16 (
  input  clock,
  input  reset,
  input  [15:0] dIn,
  output [14:0] addr,
  output wr,
  output [15:0] dOut,
  output rd
);

  wire controlunit_1_p4, controlunit_1_p5, controlunit_1_p6, controlunit_1_p9, controlunit_1_p10,
       controlunit_1_p11, controlunit_1_p12, controlunit_1_p15, controlunit_1_p16, controlunit_1_p17,
       controlunit_1_p18, controlunit_1_p19, controlunit_1_p20, controlunit_1_p24, controlunit_1_p25;
  wire [0:0] ALU_r, not_1_out;
  wire [1:0] controlunit_1_p13;
  wire [3:0] controlunit_1_p14, controlunit_1_p22, controlunit_1_p23;
  wire [15:0] adapt_1_p9, adapt_1_p10, bytes_1_tord, multiplexer_1_out, multiplexer_2_out, registerfile_1_da,
       registerfile_1_db;

  // controlUnit controlunit_1: pin names not known; wires that end beside it: clock, reset, dIn, controlunit_1_p4, controlunit_1_p5, controlunit_1_p6, wr, rd, controlunit_1_p9, controlunit_1_p10, controlunit_1_p11, controlunit_1_p12, controlunit_1_p13, controlunit_1_p14, controlunit_1_p15, controlunit_1_p16, controlunit_1_p17, controlunit_1_p18, controlunit_1_p19, controlunit_1_p20, controlunit_1_p14, controlunit_1_p22, controlunit_1_p23, controlunit_1_p24, controlunit_1_p25
  not not_1 (not_1_out[0], controlunit_1_p6);
  Multiplexer #(.Bits(16)) multiplexer_1 (
    .sel(controlunit_1_p25), .in_0({addr, ALU_r[0]}), .in_1({{15{1'b0}}, not_1_out[0]}),
    .out(multiplexer_1_out));
  Multiplexer #(.Bits(16)) multiplexer_2 (
    .sel(controlunit_1_p24), .in_0(multiplexer_1_out), .in_1(bytes_1_tord), .out(multiplexer_2_out));
  RegisterFile #(.AddrBits(4), .Bits(16)) registerfile_1 (
    .Din(multiplexer_2_out), .we(controlunit_1_p20), .Rw(controlunit_1_p14), .C(clock),
    .Ra(controlunit_1_p22), .Rb(controlunit_1_p23), .Da(registerfile_1_da), .Db(registerfile_1_db));
  // adapt adapt_1: pin names not known; wires that end beside it: registerfile_1_da, registerfile_1_db, controlunit_1_p23, controlunit_1_p15, controlunit_1_p16, controlunit_1_p17, controlunit_1_p18, controlunit_1_p19, adapt_1_p9, adapt_1_p10, controlunit_1_p4
  bytes bytes_1 (
    .dIn(dIn), .sign(controlunit_1_p9), .word(controlunit_1_p10), .A0(ALU_r[0]), .fromRS2(registerfile_1_db),
    .dOut(dOut), .toRD(bytes_1_tord));
  alu ALU (
    .R({addr, ALU_r[0]}), .A(adapt_1_p9), .B(adapt_1_p10), .sub(controlunit_1_p11),
    .logSelect(controlunit_1_p13), .\logic (controlunit_1_p12), .NE(controlunit_1_p5), .GE(controlunit_1_p6));

  // Notes on the sheet:
  //   addr: selects a 16 bit word in memory to be read or changed
  //   wr: indicates a write operation
  //   dOut: word to be sent to memory
  //   reset: when high prepares the processor to execute from address 0
  //   dIn: word coming from memory
  //   rd: indicates that memory will be read in this cycle
endmodule
