// Digital circuit system.dig as structural Verilog
// A simple system with a drv16 processor, 64KB of RAM, a terminal and keyboard
module system (
  input  clk
);

  wire and_1_out, and_2_out, comparator_1_eq, cpu_rd, cpu_wr, reset_out;
  wire [14:0] cpu_addr;
  wire [15:0] cpu_dout, keyboard_1_d, multiplexer_1_out, ramdualport_1_d;

  Keyboard keyboard_1 (.C(clk), .en(and_1_out), .D(keyboard_1_d));  // open: av
  DipSwitch reset (.out(reset_out));
  Multiplexer #(.Bits(16)) multiplexer_1 (
    .sel(comparator_1_eq), .in_0(ramdualport_1_d), .in_1(keyboard_1_d), .out(multiplexer_1_out));
  drv16 cpu (
    .clock(clk), .reset(reset_out), .dIn(multiplexer_1_out), .addr(cpu_addr), .wr(cpu_wr), .dOut(cpu_dout),
    .rd(cpu_rd));
  and and_1 (and_1_out, cpu_rd, comparator_1_eq);
  Comparator #(.Bits(15)) comparator_1 (.a({15{1'b1}}), .b(cpu_addr), .eq(comparator_1_eq));  // open: gt, lt
  RAMDualPort #(.AddrBits(15), .isProgramMemory("true"), .Bits(16)) ramdualport_1 (
    .A(cpu_addr), .Din(cpu_dout), .str(cpu_wr), .C(clk), .ld(cpu_rd), .D(ramdualport_1_d));
  and and_2 (and_2_out, comparator_1_eq, cpu_wr);
  Terminal terminal_1 (.D(cpu_dout), .C(clk), .en(and_2_out));
endmodule
